// Logisim project 1bit_AU.circ as structural Verilog: 2 circuits, main circuit main
module main (
  input  X,
  input  Y,
  input  Cin,
  output Cout,
  output G
);

  FullAdder fulladder_1 (.A(X), .B(Y), .C_in(Cin), .C_out(Cout), .S(G));
endmodule

module FullAdder (
  input  A,
  input  B,
  input  C_in,
  output C_out,
  output S
);

  wire and_1_out, and_2_out, xor_1_out;

  and and_1 (and_1_out, A, B);
  xor xor_1 (xor_1_out, A, B);
  and and_2 (and_2_out, xor_1_out, C_in);
  xor xor_2 (S, xor_1_out, C_in);
  or or_1 (C_out, and_1_out, and_2_out);
endmodule
