// Logisim project 1bit_logical_unit.circ as structural Verilog: 1 circuit, main circuit main
module main (
  input  A,
  input  B,
  input  S0,
  input  S1,
  output Y
);

  wire and_1_out, and_2_out, and_3_out, and_4_out, and_5_out, nand_1_out, not_1_out, not_2_out, not_3_out,
       not_4_out, or_1_out, xor_1_out;

  and and_1 (and_1_out, A, B);
  or or_1 (or_1_out, A, B);
  xor xor_1 (xor_1_out, A, B);
  nand nand_1 (nand_1_out, A, A);
  not not_1 (not_1_out, S0);
  not not_2 (not_2_out, S1);
  not not_3 (not_3_out, S1);
  not not_4 (not_4_out, S0);
  and and_2 (and_2_out, not_1_out, and_1_out, not_2_out);
  and and_3 (and_3_out, S0, or_1_out, not_3_out);
  and and_4 (and_4_out, not_4_out, xor_1_out, S1);
  and and_5 (and_5_out, S0, nand_1_out, S1);
  ExactlyOne xor_2 (.out(Y), .in0(and_2_out), .in1(and_3_out), .in2(and_4_out), .in3(and_5_out));
endmodule
