// Logisim project 4bit_ALU.circ as structural Verilog: 13 circuits, main circuit Arithmetic Unit (4bit)
module Arithmetic_Unit__4bit (
  input  Cin,
  input  [3:0] X,
  input  [3:0] Y,
  input  [1:0] Opcode,
  output [3:0] out_5,
  output Cout
);

  wire arithmetic_unit_1bit_1_cout, arithmetic_unit_1bit_2_cout, arithmetic_unit_1bit_3_cout;
  wire [3:0] b_input_logic_4bit_1_out_3;

  B_Input_logic__4bit b_input_logic_4bit_1 (.B(Y), .Opcode(Opcode), .out_3(b_input_logic_4bit_1_out_3));
  Arithmetic_Unit__1bit arithmetic_unit_1bit_1 (
    .X(X[0]), .Y(b_input_logic_4bit_1_out_3[0]), .Cin(Cin), .Cout(arithmetic_unit_1bit_1_cout), .G(out_5[0]));
  Arithmetic_Unit__1bit arithmetic_unit_1bit_2 (
    .X(X[1]), .Y(b_input_logic_4bit_1_out_3[1]), .Cin(arithmetic_unit_1bit_1_cout),
    .Cout(arithmetic_unit_1bit_2_cout), .G(out_5[1]));
  Arithmetic_Unit__1bit arithmetic_unit_1bit_3 (
    .X(X[2]), .Y(b_input_logic_4bit_1_out_3[2]), .Cin(arithmetic_unit_1bit_2_cout),
    .Cout(arithmetic_unit_1bit_3_cout), .G(out_5[2]));
  Arithmetic_Unit__1bit arithmetic_unit_1bit_4 (
    .X(X[3]), .Y(b_input_logic_4bit_1_out_3[3]), .Cin(arithmetic_unit_1bit_3_cout), .Cout(Cout), .G(out_5[3]));
endmodule

module Arithmetic_Unit__1bit (
  input  Cin,
  input  X,
  input  Y,
  output G,
  output Cout
);

  FullAdder fulladder_1 (.A(X), .B(Y), .C_in(Cin), .C_out(Cout), .S(G));
endmodule

module FullAdder (
  input  A,
  input  B,
  input  C_in,
  output C_out,
  output S
);

  wire and_1_out, and_2_out, xor_1_out;

  and and_1 (and_1_out, A, B);
  xor xor_1 (xor_1_out, A, B);
  and and_2 (and_2_out, xor_1_out, C_in);
  xor xor_2 (S, xor_1_out, C_in);
  or or_1 (C_out, and_1_out, and_2_out);
endmodule

module Ripple_Adder (
  input  A3,
  input  B3,
  input  A2,
  input  B2,
  input  A1,
  input  B1,
  input  A0,
  input  B0,
  input  C_in,
  output C_out,
  output S3,
  output S2,
  output S1,
  output S0
);

  wire and_1_out, and_2_out, and_3_out, and_4_out, and_5_out, and_6_out, and_7_out, and_8_out, or_2_out,
       or_3_out, or_4_out, xor_1_out, xor_2_out, xor_3_out, xor_4_out;

  and and_1 (and_1_out, A3, B3);
  xor xor_1 (xor_1_out, A3, B3);
  and and_2 (and_2_out, A2, B2);
  xor xor_2 (xor_2_out, A2, B2);
  and and_3 (and_3_out, A1, B1);
  xor xor_3 (xor_3_out, A1, B1);
  and and_4 (and_4_out, A0, B0);
  xor xor_4 (xor_4_out, A0, B0);
  and and_5 (and_5_out, xor_1_out, or_2_out);
  xor xor_5 (S3, xor_1_out, or_2_out);
  and and_6 (and_6_out, xor_2_out, or_3_out);
  xor xor_6 (S2, xor_2_out, or_3_out);
  and and_7 (and_7_out, xor_3_out, or_4_out);
  xor xor_7 (S1, xor_3_out, or_4_out);
  and and_8 (and_8_out, xor_4_out, C_in);
  xor xor_8 (S0, xor_4_out, C_in);
  or or_1 (C_out, and_1_out, and_5_out);
  or or_2 (or_2_out, and_2_out, and_6_out);
  or or_3 (or_3_out, and_3_out, and_7_out);
  or or_4 (or_4_out, and_4_out, and_8_out);
endmodule

module Half_Adder (
  input  A,
  input  B,
  output C,
  output S
);

  and and_1 (C, A, B);
  xor xor_1 (S, A, B);
endmodule

module Logical_Unit__1bit (
  input  A,
  input  B,
  input  S0,
  input  S1,
  output Y
);

  wire and_1_out, and_2_out, and_3_out, and_4_out, and_5_out, nand_1_out, not_1_out, not_2_out, not_3_out,
       not_4_out, or_1_out, xor_1_out;

  and and_1 (and_1_out, A, B);
  or or_1 (or_1_out, A, B);
  xor xor_1 (xor_1_out, A, B);
  nand nand_1 (nand_1_out, A, A);
  not not_1 (not_1_out, S0);
  not not_2 (not_2_out, S1);
  not not_3 (not_3_out, S1);
  not not_4 (not_4_out, S0);
  and and_2 (and_2_out, not_1_out, and_1_out, not_2_out);
  and and_3 (and_3_out, S0, or_1_out, not_3_out);
  and and_4 (and_4_out, not_4_out, xor_1_out, S1);
  and and_5 (and_5_out, S0, nand_1_out, S1);
  ExactlyOne xor_2 (.out(Y), .in0(and_2_out), .in1(and_3_out), .in2(and_4_out), .in3(and_5_out));
endmodule

module Logical_Unit__4bit (
  input  [3:0] B,
  input  [3:0] A,
  input  [1:0] Opcode,
  output [3:0] Lout
);

  Logical_Unit__1bit logical_unit_1bit_1 (.A(A[0]), .B(B[0]), .S0(Opcode[0]), .S1(Opcode[1]), .Y(Lout[0]));
  Logical_Unit__1bit logical_unit_1bit_2 (.A(A[1]), .B(B[1]), .S0(Opcode[0]), .S1(Opcode[1]), .Y(Lout[1]));
  Logical_Unit__1bit logical_unit_1bit_3 (.A(A[2]), .B(B[2]), .S0(Opcode[0]), .S1(Opcode[1]), .Y(Lout[2]));
  Logical_Unit__1bit logical_unit_1bit_4 (.A(A[3]), .B(B[3]), .S0(Opcode[0]), .S1(Opcode[1]), .Y(Lout[3]));
endmodule

module ALU__4bit (
  input  [3:0] A,
  input  [3:0] B,
  input  Cin,
  input  [1:0] Opcode,
  input  Mode,
  output [3:0] out_6,
  output Cout
);

  wire alu_1bit_1_cout, alu_1bit_2_cout, alu_1bit_3_cout;

  ALU__1bit alu_1bit_1 (
    .A(A[0]), .B(B[0]), .S0(Opcode[0]), .S1(Opcode[1]), .S2(Mode), .Cin(Cin), .Cout(alu_1bit_1_cout),
    .G(out_6[0]));
  ALU__1bit alu_1bit_2 (
    .A(A[1]), .B(B[1]), .S0(Opcode[0]), .S1(Opcode[1]), .S2(Mode), .Cin(alu_1bit_1_cout),
    .Cout(alu_1bit_2_cout), .G(out_6[1]));
  ALU__1bit alu_1bit_3 (
    .A(A[2]), .B(B[2]), .S0(Opcode[0]), .S1(Opcode[1]), .S2(Mode), .Cin(alu_1bit_2_cout),
    .Cout(alu_1bit_3_cout), .G(out_6[2]));
  ALU__1bit alu_1bit_4 (
    .A(A[3]), .B(B[3]), .S0(Opcode[0]), .S1(Opcode[1]), .S2(Mode), .Cin(alu_1bit_3_cout), .Cout(Cout),
    .G(out_6[3]));
endmodule

module B_Input_Logic__1bit (
  input  B,
  input  S0,
  input  S1,
  output Y
);

  wire and_1_out, and_2_out, and_3_out, and_4_out, not_1_out, not_2_out, not_3_out, not_4_out, not_5_out;

  not not_1 (not_1_out, B);
  not not_2 (not_2_out, S0);
  not not_3 (not_3_out, S1);
  not not_4 (not_4_out, S1);
  not not_5 (not_5_out, S0);
  and and_1 (and_1_out, not_2_out, 1'b0, not_3_out);
  and and_2 (and_2_out, S0, B, not_4_out);
  and and_3 (and_3_out, not_5_out, not_1_out, S1);
  and and_4 (and_4_out, S0, 1'b1, S1);
  ExactlyOne xor_1 (.out(Y), .in0(and_1_out), .in1(and_2_out), .in2(and_3_out), .in3(and_4_out));
endmodule

module B_Input_logic__4bit (
  input  [3:0] B,
  input  [1:0] Opcode,
  output [3:0] out_3
);

  B_Input_Logic__1bit b_input_logic_1bit_1 (.B(B[0]), .S0(Opcode[0]), .S1(Opcode[1]), .Y(out_3[0]));
  B_Input_Logic__1bit b_input_logic_1bit_2 (.B(B[1]), .S0(Opcode[0]), .S1(Opcode[1]), .Y(out_3[1]));
  B_Input_Logic__1bit b_input_logic_1bit_3 (.B(B[2]), .S0(Opcode[0]), .S1(Opcode[1]), .Y(out_3[2]));
  B_Input_Logic__1bit b_input_logic_1bit_4 (.B(B[3]), .S0(Opcode[0]), .S1(Opcode[1]), .Y(out_3[3]));
endmodule

module ALU__1bit (
  input  Cin,
  input  A,
  input  B,
  input  S0,
  input  S1,
  input  S2,
  output Cout,
  output G
);

  wire and_1_out, and_2_out, arithmetic_unit_1bit_1_g, b_input_logic_1bit_1_y, logical_unit_1bit_1_y,
       not_1_out;

  Arithmetic_Unit__1bit arithmetic_unit_1bit_1 (
    .X(A), .Y(b_input_logic_1bit_1_y), .Cin(Cin), .Cout(Cout), .G(arithmetic_unit_1bit_1_g));
  B_Input_Logic__1bit b_input_logic_1bit_1 (.B(B), .S0(S0), .S1(S1), .Y(b_input_logic_1bit_1_y));
  Logical_Unit__1bit logical_unit_1bit_1 (.A(A), .B(B), .S0(S0), .S1(S1), .Y(logical_unit_1bit_1_y));
  not not_1 (not_1_out, S2);
  and and_1 (and_1_out, arithmetic_unit_1bit_1_g, S2);
  and and_2 (and_2_out, logical_unit_1bit_1_y, not_1_out);
  xor xor_1 (G, and_1_out, and_2_out);
endmodule

module _2_1_Mux (
  input  A,
  input  Out,
  input  B,
  input  S2
);

  wire and_1_out, and_2_out, not_1_out;

  not not_1 (not_1_out, S2);
  and and_1 (and_1_out, A, S2);
  and and_2 (and_2_out, B, not_1_out);
  xor xor_1 (Out, and_1_out, and_2_out);
endmodule

module Main (
  input  Cin,
  input  [3:0] A,
  input  [3:0] B,
  input  [1:0] Opcode,
  input  Mode,
  output [3:0] G,
  output Cout
);

  ALU__4bit alu_4bit_1 (.A(A), .B(B), .Opcode(Opcode), .Mode(Mode), .Cin(Cin), .Cout(Cout), .out_6(G));
endmodule
