// Logisim project 4bit_logical_unit.circ as structural Verilog: 2 circuits, main circuit main
module main (
  input  [3:0] A,
  input  [3:0] B,
  input  [1:0] Opcode,
  output [3:0] Lout
);

  logicalunit L1 (.A(A[0]), .B(B[0]), .S0(Opcode[0]), .S1(Opcode[1]), .Y(Lout[0]));
  logicalunit L1_2 (.A(A[1]), .B(B[1]), .S0(Opcode[0]), .S1(Opcode[1]), .Y(Lout[1]));
  logicalunit L2 (.A(A[2]), .B(B[2]), .S0(Opcode[0]), .S1(Opcode[1]), .Y(Lout[2]));
  logicalunit L3 (.A(A[3]), .B(B[3]), .S0(Opcode[0]), .S1(Opcode[1]), .Y(Lout[3]));
endmodule

module logicalunit (
  input  A,
  input  B,
  input  S0,
  input  S1,
  output Y
);

  wire and_1_out, and_2_out, and_3_out, and_4_out, and_5_out, nand_1_out, not_1_out, not_2_out, not_3_out,
       not_4_out, or_1_out, xor_1_out;

  and and_1 (and_1_out, A, B);
  or or_1 (or_1_out, A, B);
  xor xor_1 (xor_1_out, A, B);
  nand nand_1 (nand_1_out, A, A);
  not not_1 (not_1_out, S0);
  not not_2 (not_2_out, S1);
  not not_3 (not_3_out, S1);
  not not_4 (not_4_out, S0);
  and and_2 (and_2_out, not_1_out, and_1_out, not_2_out);
  and and_3 (and_3_out, S0, or_1_out, not_3_out);
  and and_4 (and_4_out, not_4_out, xor_1_out, S1);
  and and_5 (and_5_out, S0, nand_1_out, S1);
  ExactlyOne xor_2 (.out(Y), .in0(and_2_out), .in1(and_3_out), .in2(and_4_out), .in3(and_5_out));
endmodule
