// Logisim project Multiplexer.circ as structural Verilog: 1 circuit, main circuit main
module main (
  input  x1,
  input  x2,
  input  s,
  output y
);

  wire and_1_out, and_2_out, not_1_out;

  not not_1 (not_1_out, s);
  and and_1 (and_1_out, x1, not_1_out);
  and and_2 (and_2_out, x2, s);
  xor xor_1 (y, and_1_out, and_2_out);
endmodule
