// Logisim project nBit_B_Input_Logic.circ as structural Verilog: 2 circuits, main circuit main
module main (
  input  [3:0] B,
  input  [1:0] Opcode,
  output [3:0] out_3
);

  B_Input_Logic b_input_logic_1 (.B(B[0]), .S0(Opcode[0]), .S1(Opcode[1]), .Y(out_3[0]));
  B_Input_Logic b_input_logic_2 (.B(B[1]), .S0(Opcode[0]), .S1(Opcode[1]), .Y(out_3[1]));
  B_Input_Logic b_input_logic_3 (.B(B[2]), .S0(Opcode[0]), .S1(Opcode[1]), .Y(out_3[2]));
  B_Input_Logic b_input_logic_4 (.B(B[3]), .S0(Opcode[0]), .S1(Opcode[1]), .Y(out_3[3]));
endmodule

module B_Input_Logic (
  input  B,
  input  S0,
  input  S1,
  output Y
);

  wire and_1_out, and_2_out, and_3_out, and_4_out, not_1_out, not_2_out, not_3_out, not_4_out, not_5_out;

  not not_1 (not_1_out, B);
  not not_2 (not_2_out, S0);
  not not_3 (not_3_out, S1);
  not not_4 (not_4_out, S1);
  not not_5 (not_5_out, S0);
  and and_1 (and_1_out, not_2_out, 1'b0, not_3_out);
  and and_2 (and_2_out, S0, B, not_4_out);
  and and_3 (and_3_out, not_5_out, not_1_out, S1);
  and and_4 (and_4_out, S0, 1'b1, S1);
  ExactlyOne xor_1 (.out(Y), .in0(and_1_out), .in1(and_2_out), .in2(and_3_out), .in3(and_4_out));
endmodule
